# Fritzing sketch bell (saved by Fritzing 0.9.2b)
circuit board: 4.56593cm x 5.63503cm

parts:
  Part1 = Arduino Nano (Rev3.0)
  U1 = ESP8266 WiFi Module [part_number=ESP8266]
  J1 = Basic Servo
  VCC1 = Battery
  U4 = Voltage Regulator - 3.3V [package="TO220 [THT]"]  # not connected

nets:
  N1: Part1.D1/TX, U1.RXD
  N2: Part1.D0/RX, U1.TXD
  GND: Part1.GND, U1.GND, J1.gnd, VCC1.-
  N3: Part1.D3, J1.pulse
  N4: Part1.VIN, VCC1.+
  VCC: Part1.3V3, U1.VCC, U1.CH_PD, J1.vcc

custom parts:
  ESP8266 WiFi Module: Generic WiFi Module based on the ESP8266 with onboard PCB antenna and UART communications

// code stored in the sketch: weheartit_bell.ino

